# Fritzing sketch Christmas Lights (saved by Fritzing 0.9.3b)
breadboards: 1

parts:
  R1 = Resistor [tolerance=±1% resistance=100 package=THT]
  R2 = Resistor [tolerance=±1% resistance=1k package=THT]
  Arduino_UNO_R3 = Arduino Uno (Rev3)
  Q1 = NPN-Transistor [package="TO92 [THT]"]
  LEDn = LED - 5mm [color="Green (565nm)" package="5 mm [THT]"]
  LED1 = LED - 5mm [color="Red (633nm)" package="5 mm [THT]"]
  LED2 = LED - 5mm [color="Green (565nm)" package="5 mm [THT]"]
  LED3 = LED - 5mm [color="Red (633nm)" package="5 mm [THT]"]

nets:
  N1: R1.Pin_0, Q1.C
  N2: R1.Pin_1, LEDn.anode, LED1.anode, LED2.anode, LED3.anode
  N3: R2.Pin_0, Arduino_UNO_R3.D9_PWM
  N4: R2.Pin_1, Q1.B
  GND: Arduino_UNO_R3.GND, Q1.E
  N5: Arduino_UNO_R3.VIN, LEDn.cathode, LED1.cathode, LED2.cathode, LED3.cathode

notes:
  Morse Code Christmas Lights, Drawn By: Courtney Pitcher (igniparoustempest.github.io), 1.0
